// Logisim project FloatingPointAdder.circ as structural Verilog: 5 circuits, main circuit 1 bit right shifter
module _1_bit_right_shifter (
  input  [31:0] in_1,
  output [31:0] out_2
);


  assign out_2 = {1'b0, in_1[31:1]};
endmodule

module _2_bit_right_shifter (
  input  [31:0] in_1,
  output [31:0] out_2
);

  wire [31:0] n1_bit_right_shifter_1_out_2;

  _1_bit_right_shifter u_1_bit_right_shifter_1 (.in_1(in_1), .out_2(n1_bit_right_shifter_1_out_2));
  _1_bit_right_shifter u_1_bit_right_shifter_2 (.in_1(n1_bit_right_shifter_1_out_2), .out_2(out_2));
endmodule

module _4_bit_right_shifter (
  input  [31:0] in_1,
  output [31:0] out_2
);

  wire [31:0] n2_bit_right_shifter_1_out_2;

  _2_bit_right_shifter u_2_bit_right_shifter_1 (.in_1(in_1), .out_2(n2_bit_right_shifter_1_out_2));
  _2_bit_right_shifter u_2_bit_right_shifter_2 (.in_1(n2_bit_right_shifter_1_out_2), .out_2(out_2));
endmodule

module _8_bit_right_shifter (
  input  [31:0] in_1,
  output [31:0] out_2
);

  wire [31:0] n4_bit_right_shifter_1_out_2;

  _4_bit_right_shifter u_4_bit_right_shifter_1 (.in_1(in_1), .out_2(n4_bit_right_shifter_1_out_2));
  _4_bit_right_shifter u_4_bit_right_shifter_2 (.in_1(n4_bit_right_shifter_1_out_2), .out_2(out_2));
endmodule

module _16_bit_right_shifter (
  input  [31:0] in_1,
  output [31:0] out_2
);

  wire [31:0] n8_bit_right_shifter_1_out_2;

  _8_bit_right_shifter u_8_bit_right_shifter_1 (.in_1(in_1), .out_2(n8_bit_right_shifter_1_out_2));
  _8_bit_right_shifter u_8_bit_right_shifter_2 (.in_1(n8_bit_right_shifter_1_out_2), .out_2(out_2));
endmodule
